// Logisim project DecodificadorGray.circ as structural Verilog: 1 circuit, main circuit main
module main (
  input  in_1,
  input  in_2,
  input  in_3
);

  wire xor_1_out, xor_2_out, xor_3_out;

  LED led_1 (.in(in_1));
  xor xor_1 (xor_1_out, in_1, in_2);
  LED led_2 (.in(xor_1_out));
  xor xor_2 (xor_2_out, in_2, in_3);
  xor xor_3 (xor_3_out, xor_2_out, in_1);
  LED led_3 (.in(xor_3_out));
endmodule
