// Digital circuit componente2.dig as structural Verilog
module componente2 (
  input  A,
  input  B,
  input  C,
  output D,
  output E
);

  Componente2 #(.applicationType("GHDL")) u_Componente2 (.a(A), .b(B), .c(C), .d(D), .e(E));
endmodule

/* Test case:
A B C D E
0 0 0 0 0
0 0 1 1 1
0 1 0 1 1
0 1 1 1 0
1 0 0 0 1
1 0 1 0 0
1 1 0 0 0
1 1 1 1 1
*/

/* Code of Componente2:
library ieee;
use ieee.std_logic_1164.all;

entity Componente2 is
    port(
        a, b, c: in std_logic;
        d, e: out std_logic
    );
end Componente2;

architecture behav_componente2 of Componente2 is

    signal x, y, z, w: std_logic;

    begin
        x <= (not a) AND b;
        y <= (not a) AND c;
        z <= b AND c;
        w <= a XOR b;

        d <= x OR y OR z;
        e <= w XOR c;
end behav_componente2;
*/
