// Digital circuit or4Inputs.dig as structural Verilog
module or4Inputs (
  input  in_1,
  input  in_2,
  input  in_4,
  input  in_5,
  output out_3
);

  OR4 #(.applicationType("GHDL")) u_OR4 (.a(in_1), .b(in_4), .c(in_2), .d(in_5), .s(out_3));
endmodule

/* Code of OR4:
library ieee;
use ieee.std_logic_1164.all;

entity OR4 is
    port(
        a, b, c, d: in std_logic;
        s: out std_logic
    );
end OR4;

architecture behav_OR of OR4 is
    begin
        s <= a OR b OR c OR d;
end behav_OR;
*/
