// Logisim project CodificadorGray.circ as structural Verilog: 1 circuit, main circuit main
module main (
  input  in_1,
  input  in_2,
  input  in_3
);

  wire xor_1_out, xor_2_out;

  LED led_1 (.in(in_1));
  xor xor_1 (xor_1_out, in_1, in_2);
  LED led_2 (.in(xor_1_out));
  xor xor_2 (xor_2_out, in_2, in_3);
  LED led_3 (.in(xor_2_out));
endmodule
