// Digital circuit bitadder.dig as structural Verilog
module bitadder (
  input  in_1,
  input  in_2,
  input  in_4,
  output out_3
);

  porta_and #(.applicationType("GHDL")) u_porta_and (.a(in_1), .b(in_4), .c(in_2), .s(out_3));
endmodule

/* Code of porta_and:
library ieee;
use ieee.std_logic_1164.all;

entity porta_and is
	port(
		a, b, c: in std_logic;
		s: out std_logic
	);
end porta_and;


architecture arq_and of porta_and is
begin
	process(a, b)
	begin
		if((a AND b) = '1') then
			s <= '1';
		else
			s <= '0';
		end if;
	end process;
end arq_and;
*/
