// Digital circuit full_adder.dig as structural Verilog
module full_adder (
  input  a,
  input  b,
  output carry,
  output sum
);

  half_add #(.applicationType("GHDL")) u_half_add (.a(a), .b(b), .carry(carry), .sum(sum));
endmodule

/* Test case:
a b carry sum
0 0 0 0
0 1 0 1
1 0 0 1
1 1 1 0
*/

/* Code of half_add:
library ieee;
use ieee.std_logic_1164.all;

entity half_add is
    port(
        a, b: in std_logic;
        carry, sum: out std_logic
    );
    end half_add;

architecture behav_add of half_add is
    begin
        carry <= a AND b;
        sum <= a XOR b;
    end behav_add;
*/
