// Digital circuit componente1.dig as structural Verilog
module componente1 (
  input  [3:0] in_1,
  output out_2
);

  OR4 #(.applicationType("GHDL")) u_OR4 (.a(in_1), .s(out_2));
endmodule

/* Code of OR4:
library ieee;
use ieee.std_logic_1164.all;

entity OR4 is
    port(
        a: in std_logic_vector(3 downto 0);
        s: out std_logic
    );
end OR4;

architecture behav_OR of OR4 is
    begin
        s <= a(0) OR a(1) OR a(2) OR a(3);
end behav_OR;
*/
