// Digital circuit disp_arbitro.dig as structural Verilog
module disp_arbitro (
  input  rec0,
  input  rec1,
  input  rec2,
  input  reset,
  input  clock
);

  wire u_arbitro_aut0, u_arbitro_aut1, u_arbitro_aut2, u_disp0_out_aut, u_disp0_out_rec, u_disp1_out_aut,
       u_disp1_out_rec, u_disp2_out_aut, u_disp2_out_rec;

  disp0 #(.applicationType("GHDL")) u_disp0 (
    .in_rec(rec0), .in_aut(u_arbitro_aut0), .out_rec(u_disp0_out_rec), .out_aut(u_disp0_out_aut));
  disp1 #(.applicationType("GHDL")) u_disp1 (
    .in_rec(rec1), .in_aut(u_arbitro_aut1), .out_rec(u_disp1_out_rec), .out_aut(u_disp1_out_aut));
  disp2 #(.applicationType("GHDL")) u_disp2 (
    .in_rec(rec2), .in_aut(u_arbitro_aut2), .out_rec(u_disp2_out_rec), .out_aut(u_disp2_out_aut));
  LED aut0 (.in(u_disp0_out_aut));
  LED aut1 (.in(u_disp1_out_aut));
  LED aut2 (.in(u_disp2_out_aut));
  arbitro #(.applicationType("GHDL")) u_arbitro (
    .rec0(u_disp0_out_rec), .rec1(u_disp1_out_rec), .rec2(u_disp2_out_rec), .reset(reset), .clock(clock),
    .aut0(u_arbitro_aut0), .aut1(u_arbitro_aut1), .aut2(u_arbitro_aut2));
endmodule

/* Code of disp0:
library ieee;
use ieee.std_logic_1164.all;

entity disp0 is
    port(
        in_rec, in_aut: in std_logic;
        out_rec, out_aut: out std_logic
    );
end disp0;

architecture behav_disp of disp0 is
    begin
        process (in_aut, in_rec)
        begin

            out_rec <= in_rec;

            if ((in_aut = '1') and (out_rec = '1'))  then
                out_aut <= '1';
            else
                out_aut <= '0';
            end if;

        end process;
end behav_disp;
*/

/* Code of disp1:
library ieee;
use ieee.std_logic_1164.all;

entity disp1 is
    port(
        in_rec, in_aut: in std_logic;
        out_rec, out_aut: out std_logic
    );
end disp1;

architecture behav_disp of disp1 is
    begin
        process (in_aut, in_rec)
        begin

            out_rec <= in_rec;

            if ((in_aut = '1') and (out_rec = '1'))  then
                out_aut <= '1';
            else
                out_aut <= '0';
            end if;

        end process;
end behav_disp;
*/

/* Code of disp2:
library ieee;
use ieee.std_logic_1164.all;

entity disp2 is
    port(
        in_rec, in_aut: in std_logic;
        out_rec, out_aut: out std_logic
    );
end disp2;

architecture behav_disp of disp2 is
    begin
        process (in_aut, in_rec)
        begin

            out_rec <= in_rec;

            if ((in_aut = '1') and (out_rec = '1'))  then
                out_aut <= '1';
            else
                out_aut <= '0';
            end if;

        end process;
end behav_disp;
*/

/* Code of arbitro:
library ieee;
use ieee.std_logic_1164.all;

entity arbitro is
    port(
        rec0, rec1, rec2, reset, clock: in std_logic;
        aut0, aut1, aut2: out std_logic
    );
end arbitro;

architecture behav_arbitro of arbitro is

    TYPE Tipo_estado IS (A, B, C, D) ;
    SIGNAL estado: Tipo_estado ;

begin

    process (rec0, rec1, rec2, reset, clock)
    begin

        if (reset = '1') then
            estado <= A;
            aut0 <= '0';
            aut1 <= '0';
            aut2 <= '0';
        elsif (Clock'EVENT AND Clock = '1') then
            case estado is

                --logica A para B, C e D
                when A =>
                    --logica A para B
                    if (rec0 = '1') then
                        aut0 <= '1';
                        aut1 <= '0';
                        aut2 <= '0';
                        estado <= B;
                    
                    --logica A para C
                    elsif (rec1 = '1') then
                        aut0 <= '0';
                        aut1 <= '1';
                        aut2 <= '0';
                        estado <= C;
                    
                    --logica A para D
                    elsif (rec2 = '1') then
                        aut0 <= '0';
                        aut1 <= '0';
                        aut2 <= '1';
                        estado <= D;
                    end if;

                --logica B para A
                when B =>
                    if (rec0 = '0') then
                        aut0 <= '0';
                        aut1 <= '0';
                        aut2 <= '0';
                        estado <= A;
                    end if;
                --logica C para A
                when C =>
                    if (rec1 = '0') then
                        aut0 <= '0';
                        aut1 <= '0';
                        aut2 <= '0';
                        estado <= A;
                    end if;
                --logica D para A
                when D =>
                    if (rec2 = '0') then
                        aut0 <= '0';
                        aut1 <= '0';
                        aut2 <= '0';
                        estado <= A;
                    end if;
            end case;
        end if;
        
    end process;

end behav_arbitro;
*/
