// Digital circuit caixa.dig as structural Verilog
module caixa (
  input  SensorCaixaB,
  input  [3:0] NivelCaixaA,
  output BombaB,
  output EletrovalvulaA
);

  Caixa #(.applicationType("GHDL")) u_Caixa (
    .caixaA(NivelCaixaA), .sensorB(SensorCaixaB), .bombaB(BombaB), .eletroA(EletrovalvulaA));
endmodule

/* Test case:
SensorCaixaB NivelCaixaA BombaB EletrovalvulaA
0 0b0000 0 1
1 0b0000 0 1
0 0b0001 1 0
1 0b0011 0 0
*/

/* Code of Caixa:
library ieee;
use ieee.std_logic_1164.all;

entity Caixa is
    port(
        caixaA: in std_logic_vector(3 downto 0);
        sensorB: in std_logic;
        bombaB, eletroA: out std_logic
    );
end Caixa;

--FIZ O CODIGO CONSIDERANDO QUE A BOMBA DA CAIXA B ESTARIA SEMPRE ATIVA
--EM RESALVA AOS CASOS DESCRITOS NA QUESTAO POIS ISSO NÃO FOI ESPECIFICADO
architecture behav_caixa of Caixa is
    begin
        PROCESS (caixaA, sensorB)
        begin
            eletroA <= '0';
            bombaB <= '1';
            if caixaA(0) = '0' then
                bombaB <= '0';
                eletroA <= '1';
            end if;
            if sensorB = '1' then
                bombaB <= '0';
            end if;
        end PROCESS;
end behav_caixa;
*/
